# Fritzing sketch L239D (saved by Fritzing 0.9.3b)
breadboards: 1

parts:
  元件2 = Arduino Uno (Rev3)
  IC1 = L293D [package=THT]
  元件3 = Bluetooth HC-05 Macho
  M1 = DC Motor
  M2 = DC Motor
  BAT1 = BC9VPC [package=bc9vpc]

nets:
  N1: 元件2.D8, IC1.In_1
  N2: 元件2.D10_PWM/SS, 元件3.TXD
  N3: 元件2.D2, IC1.In_4
  N4: 元件2.D3_PWM, IC1.Enable_1
  N5: 元件2.D4, IC1.In_3
  N6: 元件2.D6_PWM, IC1.Enable_2
  N7: 元件2.D7, IC1.In_2
  5V: 元件2.5V, 元件3.VCC
  GND: 元件2.GND, 元件3.GND
  N8: IC1.Out_1_(_Controlled_by_Enable_1_), M2.pin_2
  N9: IC1.0V, BAT1.V-
  N10: IC1.Out_2_(_Controlled_by_Enable_1_), M2.pin_1
  N11: IC1.+Vmotor, IC1.+V, BAT1.V+
  N12: IC1.Out_3_(_Controlled_by_Enable_2_), M1.pin_2
  N13: IC1.Out_4_(_Controlled_by_Enable_2_), M1.pin_1
