# Fritzing sketch mearm (saved by Fritzing 0.9.3b)
breadboards: 1

parts:
  元件1 = Arduino Uno (Rev3)
  元件2 = Thumb Joystick
  元件3 = Thumb Joystick
  元件4 = Bluetooth HC-05 Macho
  J1 = Basic Servo
  J2 = Basic Servo
  J4 = Basic Servo
  J5 = Basic Servo

nets:
  N1: 元件1.A0, 元件2.HORZ
  N2: 元件1.A1, 元件2.VERT
  N3: 元件1.A2, 元件3.HORZ
  N4: 元件1.A3, 元件3.VERT
  N5: 元件1.D9_PWM, J5.pulse
  N6: 元件1.D10_PWM/SS, 元件4.TXD
  N7: 元件1.D11_PWM/MOSI, 元件4.RXD
  GND: 元件1.GND, 元件2.GND, 元件3.GND, 元件4.GND, J1.gnd, J2.gnd, J4.gnd, J5.gnd
  N8: 元件1.D3_PWM, J1.pulse
  N9: 元件1.D5_PWM, J4.pulse
  N10: 元件1.D6_PWM, J2.pulse
  VCC: 元件1.5V, 元件2.VCC, 元件3.VCC, 元件4.VCC, J1.vcc, J2.vcc, J4.vcc, J5.vcc

notes:
  Buttom
  Left
  Right
  Front (claw)
